# Fritzing sketch schema elettrico (saved by Fritzing 0.9.5d)

parts:
  MH-ET_LIVE_ESP32_DEVKIT1 = MH-ET LIVE ESP32 DEVKIT 38 pins
  M1 = DC Motor
  M2 = DC Motor
  L298N2 = L298N DC motor driver
  ZS-042_RTC1 = ZS-042 RTC Module
  U3 = HC-SR04 [chip_label=IC package="SIP (Single Inline) [THT]"]
  DHT11_1 = DHT11 module
  GY1 = MPU-6050 Board GY-521 [form="♀ (female)" package=THT]
  Mod1 = 3S-BMS
  U4 = LM2596 step down module
  Raspberry_Pi_1 = Raspberry Pi 3 [part_number=RPI-3-V1.2]  # not connected
  U5 = SWITCH_SPDT [package=kps-1290]
  R1 = Resistor [tolerance=±5% resistance=330 package="2010 [SMD]"]
  USBTTL1 = Micro USB B Plug
  USBTTL2 = USB A Plug
  Bat1 = battery_holder_single_18650
  Bat2 = battery_holder_single_18650
  Bat3 = battery_holder_single_18650
  R2 = Resistor [tolerance=±5% resistance=1k package=THT]
  R3 = Resistor [tolerance=±5% resistance=20k package=THT]
  R4 = Resistor [tolerance=±5% resistance=7k package=THT]
  R5 = Resistor [tolerance=±5% resistance=470 package=THT]
  USBTTL3 = Micro USB B Plug
  M3 = 0.9v-5V booster usb output
  USBTTL4 = USB A Plug

nets:
  VCC: MH-ET_LIVE_ESP32_DEVKIT1.3V3, MH-ET_LIVE_ESP32_DEVKIT1.RST, ZS-042_RTC1.VCC, DHT11_1.VCC, GY1.pin1, GY1.pin7
  N1: MH-ET_LIVE_ESP32_DEVKIT1.SVP, R2.Pin_1, R3.Pin_0
  N2: MH-ET_LIVE_ESP32_DEVKIT1.IO32, R1.Pin_1, R5.Pin_0
  N3: MH-ET_LIVE_ESP32_DEVKIT1.IO33, U3.Trig
  N4: MH-ET_LIVE_ESP32_DEVKIT1.IO25, L298N2.ENB
  N5: MH-ET_LIVE_ESP32_DEVKIT1.IO26, L298N2.IN4
  N6: MH-ET_LIVE_ESP32_DEVKIT1.IO27, MH-ET_LIVE_ESP32_DEVKIT1.IO14, L298N2.IN3
  N7: MH-ET_LIVE_ESP32_DEVKIT1.GND#58, L298N2.GND, Mod1.-, U4.IN-, U4.OUT-, R4.Pin_1, M3.pin1, M3.pin4
  5V: MH-ET_LIVE_ESP32_DEVKIT1.CMD, MH-ET_LIVE_ESP32_DEVKIT1.5V, U3.Vcc, U4.OUT+
  GND: MH-ET_LIVE_ESP32_DEVKIT1.GND#64, ZS-042_RTC1.GND, U3.GND, DHT11_1.GND, GY1.pin2, R5.Pin_1
  N8: MH-ET_LIVE_ESP32_DEVKIT1.IO23, DHT11_1.DATA
  N9: MH-ET_LIVE_ESP32_DEVKIT1.IO22, ZS-042_RTC1.SDA, GY1.pin4
  N10: MH-ET_LIVE_ESP32_DEVKIT1.IO21, ZS-042_RTC1.SCL, GY1.pin3
  N11: MH-ET_LIVE_ESP32_DEVKIT1.IO19, MH-ET_LIVE_ESP32_DEVKIT1.IO18, MH-ET_LIVE_ESP32_DEVKIT1.IO5, L298N2.IN2
  N12: MH-ET_LIVE_ESP32_DEVKIT1.IO17, L298N2.IN1
  N13: MH-ET_LIVE_ESP32_DEVKIT1.IO16, MH-ET_LIVE_ESP32_DEVKIT1.IO4, L298N2.ENA
  N14: M1.pin_1, L298N2.OUT4
  N15: M1.pin_2, L298N2.OUT3
  N16: M2.pin_1, L298N2.OUT2
  N17: M2.pin_2, L298N2.OUT1
  N18: L298N2.12V, U4.IN+, U5.O, R2.Pin_0, M3.pin2
  N19: U3.Echo, R1.Pin_0
  N20: Mod1.0V, Bat3.+#0
  N21: Mod1.4.2V, Bat2.+#0, Bat3.+#1
  N22: Mod1.8.4V, Bat1.+#0, Bat2.+#1
  N23: Mod1.+, U5.P
  N24: Mod1.12.6V, Bat1.+#1
  N25: USBTTL1.usb, USBTTL2.usb
  N26: R3.Pin_1, R4.Pin_0
  N27: USBTTL3.usb, USBTTL4.usb

notes:
  Piano 1
  Piano 2
  Piano 3
  motore LEFT
  motore RIGHT

custom parts:
  MH-ET LIVE ESP32 DEVKIT 38 pins: http://mh.nodebb.com/topic/2/mh-et-live-esp32-devkit
  L298N DC motor driver: 2x DC motor driver with 78M05 positive voltage regulator (7..35 V) L298N: max 46 V, 2 A Set 5 V Enable jumper to enable 5 V regultor (needed for the L298N) and +5 V output at screw terminal or supply external +5 V at screw terminal Set ENA and/or ENB to +5 V to enable motor permanently or supply ENA and/or ENB with PWM signal IN1 and IN2 set rotation directory for motor A (OUT1/OUT2) IN2 and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
  HC-SR04: HC-SR04 ultrasound distance sensor
  DHT11 module: https://cdn-learn.adafruit.com/downloads/pdf/dht.pdf DHT11 black pcb module reference by:https://github.com/adafruit/Fritzing-Library/blob/master/parts/DHT11%20Humitidy%20and%20Temperature%20Sensor.fzpz
  MPU-6050 Board GY-521: Acelerometro y Giroscopio MPU-6050 Board GY-521
  3S-BMS: 3S-BMS LIPO battery charger / protection unit. Note pcb does not match the board as it will likely connect with wires, so pcb is 6 pads suitable for .1in header pins.
  LM2596 step down module: LM2596 DC-DC step down power supply module 3 A.
  battery_holder_single_18650: single 18650 battery holder
  0.9v-5V booster usb output: 0.9 V ~ 5 V up 5 V DC - DC booster module.
